// Logisim project riscv_single_cycle_datapath.circ as structural Verilog: 15 circuits, main circuit main
// RISC-V Single Cycle Datapath
module main (
);

  wire alu_1_p5, alu_control_unit_1_p3, control_unit_1_p2, control_unit_1_p3, control_unit_1_p4,
       control_unit_1_p5, control_unit_1_p6, control_unit_1_p7, control_unit_1_p8, mux_alusrc_1_p4,
       mux_pcsrc_1_p1, register_file_1_p6, register_file_1_p7;
  wire [31:0] adder_pc4_1_pc_plus_4, alu_1_p4, data_memory_1_p4, immediate_generator_1_p2,
       instruction_memory_1_p2, mux_pcsrc_1_p3, mux_pcsrc_1_p4, pc_1_pc, undriven;

  PC pc_1 (.pc_next(mux_pcsrc_1_p4), .pc(pc_1_pc));
  Adder_PC4 adder_pc4_1 (.pc(pc_1_pc), .four(undriven), .pc_plus_4(adder_pc4_1_pc_plus_4));
  // Instruction_Memory instruction_memory_1: pin names not known; wires that end beside it: pc_1_pc, instruction_memory_1_p2
  // Control_Unit control_unit_1: pin names not known; wires that end beside it: instruction_memory_1_p2, control_unit_1_p2, control_unit_1_p3, control_unit_1_p4, control_unit_1_p5, control_unit_1_p6, control_unit_1_p7, control_unit_1_p8
  // Mux_PCSrc mux_pcsrc_1: pin names not known; wires that end beside it: mux_pcsrc_1_p1, adder_pc4_1_pc_plus_4, mux_pcsrc_1_p3, mux_pcsrc_1_p4
  // Register_File register_file_1: pin names not known; wires that end beside it: instruction_memory_1_p2, instruction_memory_1_p2, instruction_memory_1_p2, instruction_memory_1_p2, control_unit_1_p2, register_file_1_p6, register_file_1_p7
  // Immediate_Generator immediate_generator_1: pin names not known; wires that end beside it: instruction_memory_1_p2, immediate_generator_1_p2
  // Mux_ALUSrc mux_alusrc_1: pin names not known; wires that end beside it: register_file_1_p7, immediate_generator_1_p2, control_unit_1_p3, mux_alusrc_1_p4
  Adder_Branch adder_branch_1 (
    .pc_plus_4(pc_1_pc), .branch_imm(immediate_generator_1_p2), .branch_target(mux_pcsrc_1_p3));
  // ALU_Control_Unit alu_control_unit_1: pin names not known; wires that end beside it: instruction_memory_1_p2, control_unit_1_p8, alu_control_unit_1_p3
  // ALU alu_1: pin names not known; wires that end beside it: register_file_1_p6, mux_alusrc_1_p4, alu_control_unit_1_p3, alu_1_p4, alu_1_p5
  Branch_AND branch_and_1 (.branch(control_unit_1_p7), .zero(alu_1_p5), .pc_src(mux_pcsrc_1_p1));
  // Data_Memory data_memory_1: pin names not known; wires that end beside it: alu_1_p4, control_unit_1_p4, control_unit_1_p5, data_memory_1_p4
  Mux_MemToReg mux_memtoreg_1 (
    .alu_result(alu_1_p4), .mem_read_data(data_memory_1_p4), .mem_to_reg(control_unit_1_p6),
    .write_back(instruction_memory_1_p2));

  // Notes on the sheet:
  //   RISC-V Single Cycle Datapath (Lab 14 - Simplified)
  //   Note: This is a complete editable datapath schematic/black-box wiring diagram matching the provided lab figure. Add internal memory/register-file logic as needed for simulation.
  //   4
  //   Instr[31:0]
  //   PCSrc
  //   rs1 [19:15]
  //   rs2 [24:20]
  //   rd [11:7]
  //   funct3 [14:12]
  //   funct7 [31:25]
  //   opcode [6:0]
  //   RegWrite
  //   PC + 4
  //   ALUSrc
  //   Branch Immediate (Imm << 1)
  //   ALU Control
  //   Branch
  //   Zero
  //   MemRead
  //   MemWrite
  //   MemToReg
endmodule

module PC (
  input  [31:0] pc_next,
  output [31:0] pc
);
endmodule

// Instruction Memory
module Instruction_Memory (
  input  [31:0] addr,
  output [31:0] instr
);
endmodule

// Register File
module Register_File (
  input  [4:0] rs1,
  input  [4:0] rs2,
  input  [4:0] rd,
  input  [31:0] write_data,
  input  reg_write,
  output [31:0] read_data_1,
  output [31:0] read_data_2
);
endmodule

// Immediate Generator
module Immediate_Generator (
  input  [31:0] instr,
  output [31:0] imm_ext
);
endmodule

// Control Unit
module Control_Unit (
  input  [6:0] opcode,
  output reg_write,
  output alu_src,
  output mem_read,
  output mem_write,
  output mem_to_reg,
  output branch,
  output [1:0] alu_op
);
endmodule

// Add
module Adder_PC4 (
  input  [31:0] pc,
  input  [31:0] four,
  output [31:0] pc_plus_4
);
endmodule

// Add
module Adder_Branch (
  input  [31:0] pc_plus_4,
  input  [31:0] branch_imm,
  output [31:0] branch_target
);
endmodule

// PCSrc MUX
module Mux_PCSrc (
  input  pc_src,
  input  [31:0] pc_plus_4,
  input  [31:0] branch_target,
  output [31:0] pc_next
);
endmodule

// ALUSrc MUX
module Mux_ALUSrc (
  input  alu_src,
  input  [31:0] read_data_2,
  input  [31:0] imm_ext,
  output [31:0] alu_b
);
endmodule

module ALU (
  input  [31:0] a,
  input  [31:0] b,
  input  [3:0] alu_control,
  output [31:0] result,
  output zero
);
endmodule

// Branch AND
module Branch_AND (
  input  branch,
  input  zero,
  output pc_src
);
endmodule

// Data Memory
module Data_Memory (
  input  mem_read,
  input  mem_write,
  input  [31:0] addr,
  input  [31:0] write_data,
  output [31:0] read_data
);
endmodule

// MemToReg MUX
module Mux_MemToReg (
  input  mem_to_reg,
  input  [31:0] alu_result,
  input  [31:0] mem_read_data,
  output [31:0] write_back
);
endmodule

// ALU Control Unit
module ALU_Control_Unit (
  input  [2:0] funct3,
  input  [6:0] funct7,
  input  [1:0] alu_op,
  output [3:0] alu_control
);
endmodule
